# Fritzing sketch arduino_mega_shield (saved by Fritzing 0.8.3b)
circuit board: 8.44907cm x 5.40696cm
breadboards: 1

parts:
  Arduino1 = Arduino Mega
  J8 = female pin header, 6 pins [form="♀ (female)"]
  J9 = female pin header, 6 pins [form="♀ (female)"]
  J10 = female pin header, 6 pins [form="♀ (female)"]
  J11 = female pin header, 6 pins [form="♀ (female)"]
  J12 = female pin header, 6 pins [form="♀ (female)"]
  J13 = female pin header, 2 pins [form="♀ (female)"]
  J14 = female pin header, 2 pins [form="♀ (female)"]
  J15 = female pin header, 2 pins [form="♀ (female)"]
  J16 = female pin header, 2 pins [form="♀ (female)"]
  J17 = female pin header, 2 pins [form="♀ (female)"]
  J19 = female pin header, 1 pin [form="♀ (female)"]
  J20 = female pin header, 8 pins [form="♀ (female)"]
  J21 = female pin header, 8 pins [form="♀ (female)"]
  J22 = female pin header, 8 pins [form="♀ (female)"]
  J23 = female pin header, 8 pins [form="♀ (female)"]
  J24 = female pin header, 8 pins [form="♀ (female)"]
  J25 = female pin header, 8 pins [form="♀ (female)"]
  J18 = female pin header, 3 pins [form="♀ (female)"]
  J26 = female pin header, 3 pins [form="♀ (female)"]
  J27 = female pin header, 3 pins [form="♀ (female)"]
  J28 = female pin header, 3 pins [form="♀ (female)"]
  J29 = female pin header, 3 pins [form="♀ (female)"]
  J30 = female pin header, 3 pins [form="♀ (female)"]
  J31 = female pin header, 3 pins [form="♀ (female)"]
  J32 = female pin header, 3 pins [form="♀ (female)"]
  J33 = female pin header, 3 pins [form="♀ (female)"]
  J34 = female pin header, 3 pins [form="♀ (female)"]
  J35 = female pin header, 1 pin [form="♀ (female)"]
  J36 = female pin header, 1 pin [form="♀ (female)"]
  J37 = female pin header, 1 pin [form="♀ (female)"]
  J38 = female pin header, 1 pin [form="♀ (female)"]
  J7 = female pin header, 4 pins [form="♀ (female)"]
  J39 = female pin header, 1 pin [form="♀ (female)"]
  J40 = female pin header, 1 pin [form="♀ (female)"]
  J41 = female pin header, 2 pins [form="♀ (female)"]

nets:
  N1: Arduino1.AREF, J15.pin1
  N2: Arduino1.GND, J10.pin4, J10.pin5, J15.pin2, J19.pin1, J20.pin1, J21.pin1, J22.pin1, J23.pin1, J24.pin1, J25.pin1, J35.pin1, J36.pin1, J37.pin1, J40.pin1
  N3: Arduino1.D13, J9.pin1, J20.pin3, J21.pin3, J22.pin3, J23.pin3, J24.pin3, J25.pin3
  N4: Arduino1.D12, J9.pin2, J20.pin4, J21.pin4, J22.pin4, J23.pin4, J24.pin4, J25.pin4
  N5: Arduino1.D11, J9.pin3, J20.pin5, J21.pin5, J22.pin5, J23.pin5, J24.pin5, J25.pin5
  N6: Arduino1.D10, J9.pin4, J20.pin6, J21.pin6, J22.pin6, J23.pin6, J24.pin6, J25.pin6
  N7: Arduino1.D9, J9.pin5, J20.pin7, J21.pin7, J22.pin7, J23.pin7, J24.pin7, J25.pin7
  N8: Arduino1.D8, J9.pin6, J24.pin8
  N9: Arduino1.D7, J14.pin1, J23.pin8
  N10: Arduino1.D6, J14.pin2, J22.pin8
  N11: Arduino1.D5, J8.pin1, J21.pin8
  N12: Arduino1.D4, J8.pin2, J20.pin8
  N13: Arduino1.D3, J8.pin3, J25.pin8
  N14: Arduino1.D2, J8.pin4
  N15: Arduino1.D1TX, J8.pin5
  N16: Arduino1.D0RX, J8.pin6
  N17: Arduino1.RST, J10.pin1
  N18: Arduino1.3V3, J10.pin2
  N19: Arduino1.+5V, J10.pin3, J20.pin2, J21.pin2, J22.pin2, J23.pin2, J24.pin2, J25.pin2
  N20: Arduino1.VIN, J10.pin6
  N21: Arduino1.A0, J11.pin1
  N22: Arduino1.A1, J11.pin2
  N23: Arduino1.A2, J11.pin3
  N24: Arduino1.A3, J11.pin4
  N25: Arduino1.A4, J11.pin5
  N26: Arduino1.A5, J11.pin6
  N27: Arduino1.D14, J13.pin1
  N28: Arduino1.D15, J13.pin2
  N29: Arduino1.D16, J41.pin1
  N30: Arduino1.D17, J41.pin2
  N31: Arduino1.D18, J7.pin1
  N32: Arduino1.D19, J7.pin2
  N33: Arduino1.D20, J7.pin3
  N34: Arduino1.D21, J7.pin4
  N35: Arduino1.D22, J39.pin1
  N36: Arduino1.D23, J38.pin1
  N37: Arduino1.D24, J26.pin3
  N38: Arduino1.D25, J18.pin3
  N39: Arduino1.D26, J26.pin2
  N40: Arduino1.D27, J18.pin2
  N41: Arduino1.D28, J26.pin1
  N42: Arduino1.D29, J18.pin1
  N43: Arduino1.D30, J28.pin3
  N44: Arduino1.D31, J27.pin3
  N45: Arduino1.D32, J28.pin2
  N46: Arduino1.D33, J27.pin2
  N47: Arduino1.D34, J28.pin1
  N48: Arduino1.D35, J27.pin1
  N49: Arduino1.D36, J29.pin3
  N50: Arduino1.D37, J30.pin3
  N51: Arduino1.D38, J29.pin2
  N52: Arduino1.D39, J30.pin2
  N53: Arduino1.D40, J29.pin1
  N54: Arduino1.D41, J30.pin1
  N55: Arduino1.D42, J33.pin3
  N56: Arduino1.D43, J34.pin3
  N57: Arduino1.D44, J33.pin2
  N58: Arduino1.D45, J34.pin2
  N59: Arduino1.D46, J33.pin1
  N60: Arduino1.D47, J34.pin1
  N61: Arduino1.D48, J31.pin3
  N62: Arduino1.D49, J32.pin3
  N63: Arduino1.D50, J31.pin2
  N64: Arduino1.D51, J32.pin2
  N65: Arduino1.D52, J31.pin1
  N66: Arduino1.D53, J32.pin1
  N67: Arduino1.A6, J16.pin1
  N68: Arduino1.A7, J16.pin2
  N69: Arduino1.A8, J12.pin1
  N70: Arduino1.A9, J12.pin2
  N71: Arduino1.A10, J12.pin3
  N72: Arduino1.A11, J12.pin4
  N73: Arduino1.A12, J12.pin5
  N74: Arduino1.A13, J12.pin6
  N75: Arduino1.A14, J17.pin1
  N76: Arduino1.A15, J17.pin2

notes:
  Alex Porto
